// Digital circuit gpu.dig as structural Verilog
module gpu (
  input  clk,
  input  [15:0] addr_in,
  input  draw,
  output [15:0] addr_ram,
  output [7:0] data_rom,
  output [15:0] addr_rom,
  output [7:0] data_ram
);

  wire _8bit_counter_1_ovf, _8bit_counter_2_ovf, _74138_modified_1_ny0, _74138_modified_1_ny1,
       _74138_modified_1_ny2, and_1_out, and_2_out, and_3_out, and_4_out, jk_ff_1_nq, load_3, load_4, load_5,
       not_1_out, not_2_out, not_3_out, not_4_out, not_5_out, not_6_out, not_7_out, or_1_out, or_2_out,
       or_4_out, state_char_1_p4, state_char_1_p6, state_char_1_p7, state_char_1_p8, state_char_1_p9;
  wire [1:0] _74138_modified_1_ny7;
  wire [7:0] _8bit_register_1_q, sprite_memory_d;
  wire [15:0] memory_ptr_1_out, sprite_ptr_1_out;

  sprite_ptr sprite_ptr_1 (
    .en0(or_1_out), .clk(clk), .nclr0(jk_ff_1_nq), .nclr1(jk_ff_1_nq), .en1(or_1_out), .out(sprite_ptr_1_out));
  memory_ptr memory_ptr_1 (
    .in0(data_rom), .en(not_7_out), .nld0(load_5), .in1(data_rom), .clk(clk), .nld1(load_4),
    .out(memory_ptr_1_out));
  Multiplexer #(.Selector_Bits(2), .Bits(16)) multiplexer_1 (
    .sel(_74138_modified_1_ny7), .in_0(memory_ptr_1_out), .in_1(sprite_ptr_1_out), .in_2(addr_in),
    .in_3(addr_in), .out(addr_rom));
  not not_1 (not_1_out, _74138_modified_1_ny7[0]);
  JK_FF jk_ff_1 (.J(and_1_out), .C(clk), .K(draw), .Q(_74138_modified_1_ny7[1]), .nQ(jk_ff_1_nq));
  or or_1 (or_1_out, state_char_1_p4, _74138_modified_1_ny7[0]);
  _74138_modified _74138_modified_1 (
    .A(sprite_ptr_1_out[0]), .C(sprite_ptr_1_out[2]), .B(sprite_ptr_1_out[1]), .G(1'b1), .nGB(1'b0),
    .nGA(1'b0), .nY0(_74138_modified_1_ny0), .nY1(_74138_modified_1_ny1), .nY2(_74138_modified_1_ny2),
    .nY3(load_3), .nY4(load_4), .nY5(load_5), .nY7(_74138_modified_1_ny7[0]), .VCC(1'b1), .GND(1'b0));  // open: nY6
  ROM #(.AddrBits(16), .Bits(8)) sprite_memory (.A(addr_rom), .sel(1'b1), .D(sprite_memory_d));
  assign data_rom = and_2_out ? sprite_memory_d : 8'bz;  // Driver driver_1
  not not_2 (not_2_out, _74138_modified_1_ny1);
  and and_1 (and_1_out, data_rom[0], not_3_out);
  not not_3 (not_3_out, _74138_modified_1_ny0);
  not not_4 (not_4_out, _74138_modified_1_ny2);
  _8bit_register _8bit_register_1 (.clk(clk), .D(data_rom), .en(not_2_out), .Q(_8bit_register_1_q));
  and and_2 (and_2_out, not_6_out, jk_ff_1_nq);
  not not_5 (not_5_out, or_2_out);
  not not_6 (not_6_out, state_char_1_p8);
  // state_char state_char_1: pin names not known; wires that end beside it: data_rom, not_1_out, clk, state_char_1_p4, and_2_out, state_char_1_p6, state_char_1_p7, state_char_1_p8, state_char_1_p9
  _8bit_counter _8bit_counter_1 (
    .in(_8bit_register_1_q), .en(not_1_out), .nld(not_5_out), .clk(clk), .out(addr_ram[7:0]),
    .ovf(_8bit_counter_1_ovf));
  not not_7 (not_7_out, state_char_1_p9);
  or or_2 (or_2_out, state_char_1_p6, not_4_out, _8bit_counter_1_ovf);
  or or_3 (state_char_1_p4, and_4_out, state_char_1_p7);
  _8bit_counter _8bit_counter_2 (
    .in(data_rom), .en(or_2_out), .nld(load_3), .clk(clk), .out(addr_ram[15:8]), .ovf(_8bit_counter_2_ovf));
  and and_3 (and_3_out, not_1_out, or_4_out);
  and and_4 (and_4_out, _8bit_counter_2_ovf, _8bit_counter_1_ovf);
  RAMDualPort #(.AddrBits(16), .Bits(8)) ramdualport_1 (
    .A(addr_ram), .Din(data_rom), .str(and_3_out), .C(clk), .ld(state_char_1_p8), .D(data_ram));
  or or_4 (or_4_out, state_char_1_p9, data_rom[0]);

  // Other names for the same wires on the sheet: data[7:0] = data_rom

  // Notes on the sheet:
  //   clk: Hz: 30000
  //   contents of sprite_memory (hex, n*v repeats v):
  //   c,0,ff,0,0,41,4*0,ff,0,0,40,0,0,0,50,8b,2d,6,60,0,0,0,32,50,14
  //   ,0,50,0,0,0,1e,3c,30,0,50,0,0,1,23*0,74,18,14*0,10*8,4*49,16*8
  //   ,a,6*8,4*49,e1,f5,f5,e1,49,15*8,a,7*8,49,e1,9b,9b,e1,e1,9b,9b
  //   ,49,49,13*8,a,6*8,49,e1,e1,e1,4*9b,e1,9b,9b,49,12*8,a,5*8,49,f5
  //   ,e1,e1,4*9b,e1,e1,f5,9b,9b,49,11*8,a,4*8,49,9b,f5,f5,9b,f5,e1
  //   ,f5,e1,e1,f5,f5,f5,9b,49,11*8,a,4*8,49,e1,e1,e1,7*f5,e1,e1,9b
  //   ,49,11*8,a,5*8,49,9b,4*e1,49,e1,49,9b,9b,e1,9b,9b,49,10*8,a,4*8
  //   ,9b,49,9b,e1,e1,49,49,eb,49,eb,49,49,9b,e1,9b,49,10*8,a,4*8,49
  //   ,8,49,1,49,db,db,db,49,db,db,db,1,9b,9b,49,10*8,a,4*8,49,8,8,1
  //   ,db,ff,1,eb,db,1,ff,db,1,9b,49,11*8,a,7*8,1,db,ff,1,eb,eb,1,ff
  //   ,db,1,9b,49,11*8,a,7*8,1,db,6*eb,db,1,49,12*8,a,6*8,45,45,1,db
  //   ,4*eb,db,1,45,45,12*8,a,5*8,45,ff,ef,1,1,db,eb,eb,db,1,1,ff,ef
  //   ,45,11*8,a,5*8,45,ef,ef,9f,9f,4*1,9f,45,ef,ef,45,11*8,a,4*8,5*45
  //   ,6*ef,9f,4*45,10*8,a,4*8,45,db,db,45,9f,9f,ef,ff,ff,ff,ef,9f,45
  //   ,81,db,45,10*8,a,4*8,45,45,81,1,45,9f,9f,ef,ef,ef,9f,45,1,81,45,45
  //   ,10*8,a,4*8,45,9f,45,8,1,45,4*9f,45,1,8,45,9f,45,10*8,a,4*8,45,45,45
  //   ,1,1,9f,4*45,9f,1,1,45,45,45,10*8,a,4*8,1,eb,eb,1,45,45,9f,ff
  //   ,ef,9f,45,45,1,eb,eb,1,10*8,a,4*8,1,db,db,1,81,81,4*45,81,81,1
  //   ,db,db,1,10*8,a,5*8,1,1,1,4*81,1,81,81,81,1,1,1,11*8,a,7*8,1,81
  //   ,db,81,81,1,81,81,81,1,13*8,a,7*8,1,4*81,1,81,81,81,1,13*8,a,8*8
  //   ,1,81,81,81,1,81,81,1,14*8,a,8*8,1,81,81,81,1,81,81,1,14*8,a,8*8
  //   ,1,9f,81,81,1,81,81,1,14*8,a,8*8,1,ef,ef,9f,1,9f,9f,1,14*8,a,9*8
  //   ,7*1,14*8,a,30*8,a,30*8,a,30*8,a,30*8,a,30*8,a,30*8,a,30*8,a,30*8
  //   ,a,30*8,a,30*8,a,30*8,a,30*8,a,30*8,a,30*8,a,30*8,a,30*8,a,30*8
  //   ,a,30*8,a,30*8,a,c,0,30*8,f5,f5,4*a5,ad,ad,a5,ad,ad,18*8,a,22*8
  //   ,f5,ad,ad,ed,ed,ad,5*a5,9d,9b,7*a5,5b,53,15*8,a,18*8,ad,ad,f5,f5
  //   ,ed,4*a5,9d,9b,5b,9b,5b,5b,5b,9b,9d,9d,5*a5,5b,53,15*8,a,15*8
  //   ,a3,a5,a5,a5,ad,4*a5,9d,a5,9d,6*5b,5*53,5b,9d,a5,a5,5b,5b,53,14*8
  //   ,a,14*8,a3,a5,a3,4*9b,a5,a5,9d,9b,9d,4*5b,5*53,4b,4b,4*53,5b,9b
  //   ,5b,5b,14*8,a,13*8,a3,a3,9b,9b,5b,5b,9b,9b,a3,5*9b,5b,5b,53,53
  //   ,b,b,b,8*53,5b,5b,53,53,53,12*8,a,12*8,9b,9b,9b,5b,5b,53,5b,6*9b
  //   ,5b,53,5b,5b,15*53,4*5b,11*8,a,11*8,a3,a3,9b,5b,4*53,9b,4*53,5b
  //   ,9b,9b,18*53,4*5b,10*8,a,10*8,a5,a3,5b,5b,7*53,49,4b,13*53,4b
  //   ,4*b,4b,4b,4*53,5b,5b,10*8,a,10*8,a5,9b,6*53,49,5*9,49,49,49,8*53
  //   ,4b,53,7*b,4b,53,53,53,5b,5b,9*8,a,8*8,a5,a5,9b,5*53,49,49,9,1,1,1
  //   ,9,1,1,9,8*53,4b,4b,10*b,53,5b,5b,53,53,8*8,a,8*8,ad,9b,5b,4*53
  //   ,49,9,49,9,9,1,1,9,1,1,9,49,6*53,4b,5*9,6*b,53,4b,53,5b,5b,5b
  //   ,8*8,a,7*8,ad,a5,7*53,49,49,49,9,9,9,49,9,9,9,1,49,5b,9d,5b,53,53
  //   ,4b,4b,b,b,4*9,5*b,53,53,53,5b,5b,8*8,a,7*8,a5,17*53,4*49,53,53,53
  //   ,4b,4b,10*9,b,b,b,4b,53,53,5b,53,7*8,a,6*8,a5,5b,53,53,53,5b,5b
  //   ,8*53,5*5b,7*53,4b,49,10*9,b,b,4b,4b,53,53,53,7*8,a,5*8,ed,a5
  //   ,4*9b,5b,9*9b,6*a5,9b,9b,5b,5b,53,53,53,4b,49,49,8*9,4b,4b,49,49
  //   ,53,53,5b,53,6*8,a,4*8,f7,ad,4*9b,5b,9b,9b,9b,5b,9b,a3,a5,a5,ad
  //   ,4*ed,f7,f7,ed,ed,ad,a5,a3,9b,53,51,51,4b,49,49,49,4*9,4*49,9,9
  //   ,49,49,53,5b,6*8,a,4*8,f7,a5,9b,5b,9b,9b,9b,5b,5b,53,5b,a5,ad
  //   ,ed,13*f7,ed,a5,a3,5b,53,15*49,53,5b,5b,5*8,a,4*8,a5,9b,5b,9b,9b,9b
  //   ,53,5b,9b,53,a3,ed,17*f7,ed,ed,a5,9b,9b,6*53,51,5*49,51,53,5b,5b
  //   ,5*8,a,4*8,a5,5b,9b,9b,5b,53,53,9b,53,5b,ad,20*f7,ef,ed,ad,4*a5
  //   ,9d,9b,9b,53,49,49,49,9,53,53,53,a3,a3,4*8,a,8,8,8,f7,a5,53,9b,9b
  //   ,53,53,53,9b,53,9b,ed,22*f7,ef,ef,af,5*ad,a5,9b,49,9,9,9,53,53
  //   ,9b,a3,4*8,a,8,8,8,f7,9b,53,9b,9b,53,53,5b,5b,5b,ad,6*f7,ff,ff,ff
  //   ,18*f7,5*af,ad,a5,49,49,49,4b,53,5b,a3,4*8,a,8,8,8,ad,5b,5b,a3
  //   ,9b,53,9b,9b,5b,a5,ed,5*f7,5*ff,17*f7,ef,ef,5*af,9d,53,49,4b,53,53
  //   ,a3,a3,8,8,8,a,8,8,8,a5,53,5b,9b,9b,5b,9b,5b,5b,a5,ed,4*f7,5*ff
  //   ,17*f7,4*ef,af,ef,af,af,a5,5b,4*53,a3,a3,8,8,8,a,8,8,f7,9b,53
  //   ,5b,9b,5b,9b,a3,53,5b,a5,ed,f7,f7,f7,ff,ff,f7,ff,ff,17*f7,6*ef
  //   ,af,af,af,ad,5d,4*53,5b,ad,8,8,8,a,8,8,f7,5b,53,9b,9b,5b,9b,5b
  //   ,53,5b,ad,ed,23*f7,6*ef,af,af,af,ef,ef,ad,a5,53,4b,53,53,53,ad
  //   ,8,8,8,a,8,8,ed,5b,5b,9b,9b,4*53,9b,ad,ed,22*f7,6*ef,5*af,ef,ad
  //   ,a5,53,4b,53,53,53,ad,8,8,8,a,8,8,ad,5b,5b,9b,5*53,a5,ad,ed,22*f7
  //   ,6*ef,5*af,ef,ad,a5,5b,53,49,51,53,ad,ed,8,8,a,8,8,a5,53,53,5b
  //   ,53,53,53,4b,5b,a5,ad,ed,26*f7,ef,ef,af,ad,ad,ad,af,ef,ed,a5,5b
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endmodule
