// Digital circuit gpu_nomem.dig as structural Verilog
module gpu_nomem (
  input  clk,
  input  [15:0] addr_in,
  input  start,
  input  [7:0] data,
  output [15:0] addr_ram,
  output [15:0] addr_rom,
  output store_ram,
  output load_ram,
  output load_rom
);

  wire _8bit_counter_1_ovf, _8bit_counter_2_ovf, _74138_modified_1_ny0, _74138_modified_1_ny1,
       _74138_modified_1_ny2, and_1_out, and_5_out, data_0, done, drawing, fill, load_3, load_4, load_5,
       nidling, not_1_out, not_3_out, not_4_out, not_5_out, not_6_out, not_7_out, or_1_out, or_2_out,
       or_4_out, reset, state_char_1_p6;
  wire [1:0] jk_ff_1_q;
  wire [7:0] _8bit_register_1_q;
  wire [15:0] memory_ptr_1_out, sprite_ptr_1_out;

  sprite_ptr sprite_ptr_1 (
    .en0(or_1_out), .clk(clk), .nclr0(nidling), .nclr1(nidling), .en1(or_1_out), .out(sprite_ptr_1_out));
  memory_ptr memory_ptr_1 (
    .in0(data), .en(not_1_out), .nld0(load_5), .in1(data), .clk(clk), .nld1(load_4), .out(memory_ptr_1_out));
  not not_1 (not_1_out, fill);
  Multiplexer #(.Selector_Bits(2), .Bits(16)) multiplexer_1 (
    .sel(jk_ff_1_q), .in_0(memory_ptr_1_out), .in_1(sprite_ptr_1_out), .in_2(addr_in), .in_3(addr_in),
    .out(addr_rom));
  not not_2 (drawing, jk_ff_1_q[0]);
  JK_FF jk_ff_1 (.J(and_1_out), .C(clk), .K(start), .Q(jk_ff_1_q[1]), .nQ(nidling));
  or or_1 (or_1_out, reset, jk_ff_1_q[0]);
  _74138_modified _74138_modified_1 (
    .A(sprite_ptr_1_out[0]), .C(sprite_ptr_1_out[2]), .B(sprite_ptr_1_out[1]), .G(1'b1), .nGB(1'b0),
    .nGA(1'b0), .nY0(_74138_modified_1_ny0), .nY1(_74138_modified_1_ny1), .nY2(_74138_modified_1_ny2),
    .nY3(load_3), .nY4(load_4), .nY5(load_5), .nY7(jk_ff_1_q[0]), .VCC(1'b1), .GND(1'b0));  // open: nY6
  not not_3 (not_3_out, _74138_modified_1_ny1);
  not not_4 (not_4_out, _74138_modified_1_ny0);
  not not_5 (not_5_out, _74138_modified_1_ny2);
  _8bit_register _8bit_register_1 (.clk(clk), .D(data), .en(not_3_out), .Q(_8bit_register_1_q));
  and and_1 (and_1_out, data_0, not_4_out);
  and and_2 (data_0, data[0], load_rom);
  and and_3 (load_rom, not_7_out, nidling);
  _8bit_counter _8bit_counter_1 (
    .in(_8bit_register_1_q), .en(drawing), .nld(not_6_out), .clk(clk), .out(addr_ram[7:0]),
    .ovf(_8bit_counter_1_ovf));
  not not_6 (not_6_out, or_2_out);
  not not_7 (not_7_out, load_ram);
  // state_char state_char_1: pin names not known; wires that end beside it: data, drawing, clk, reset, load_rom, state_char_1_p6, done, load_ram, fill
  or or_2 (or_2_out, state_char_1_p6, _8bit_counter_1_ovf, not_5_out);
  _8bit_counter _8bit_counter_2 (
    .in(data), .en(or_2_out), .nld(load_3), .clk(clk), .out(addr_ram[15:8]), .ovf(_8bit_counter_2_ovf));
  or or_3 (reset, and_5_out, done);
  and and_4 (store_ram, drawing, or_4_out);
  and and_5 (and_5_out, _8bit_counter_2_ovf, _8bit_counter_1_ovf);
  or or_4 (or_4_out, fill, data_0);

  // Other names for the same wires on the sheet: send = load_ram

  // Notes on the sheet:
  //   clk: Hz: 120000
endmodule
