// Digital circuit shift_reg.dig as structural Verilog
module shift_reg (
  input  [7:0] in,
  input  clk,
  input  sh_nld,
  output out
);

  _74165 _74165_1 (
    .pin1(sh_nld), .pin2(clk), .pin3(in[4]), .pin4(in[5]), .pin5(in[6]), .pin6(in[7]), .pin8(1'b0),
    .pin9(out), .pin10(1'b0), .pin11(in[0]), .pin12(in[1]), .pin13(in[2]), .pin14(in[3]), .pin15(1'b0),
    .pin16(1'b1));  // open: pin7
endmodule
