// Digital circuit sprite_ptr.dig as structural Verilog
module sprite_ptr (
  input  en0,
  input  clk,
  input  nclr0,
  input  nclr1,
  input  en1,
  output [15:0] out
);

  wire _74163_1_pin15, _74163_2_pin15, _74163_3_pin15;
  wire [7:0] _74163_1_pin3, _74163_3_pin3;

  _74163 _74163_1 (
    .pin1(nclr0), .pin2(clk), .pin3(_74163_1_pin3[0]), .pin4(_74163_1_pin3[1]), .pin5(_74163_1_pin3[2]),
    .pin6(_74163_1_pin3[3]), .pin7(en0), .pin8(1'b0), .pin9(1'b1), .pin10(1'b1), .pin11(out[3]),
    .pin12(out[2]), .pin13(out[1]), .pin14(out[0]), .pin15(_74163_1_pin15), .pin16(1'b1));
  _74163 _74163_2 (
    .pin1(nclr1), .pin2(clk), .pin3(_74163_1_pin3[4]), .pin4(_74163_1_pin3[5]), .pin5(_74163_1_pin3[6]),
    .pin6(_74163_1_pin3[7]), .pin7(en1), .pin8(1'b0), .pin9(1'b1), .pin10(_74163_1_pin15), .pin11(out[7]),
    .pin12(out[6]), .pin13(out[5]), .pin14(out[4]), .pin15(_74163_2_pin15), .pin16(1'b1));
  _74163 _74163_3 (
    .pin1(nclr1), .pin2(clk), .pin3(_74163_3_pin3[0]), .pin4(_74163_3_pin3[1]), .pin5(_74163_3_pin3[2]),
    .pin6(_74163_3_pin3[3]), .pin7(en1), .pin8(1'b0), .pin9(1'b1), .pin10(_74163_2_pin15), .pin11(out[11]),
    .pin12(out[10]), .pin13(out[9]), .pin14(out[8]), .pin15(_74163_3_pin15), .pin16(1'b1));
  _74163 _74163_4 (
    .pin1(nclr1), .pin2(clk), .pin3(_74163_3_pin3[4]), .pin4(_74163_3_pin3[5]), .pin5(_74163_3_pin3[6]),
    .pin6(_74163_3_pin3[7]), .pin7(en1), .pin8(1'b0), .pin9(1'b1), .pin10(_74163_3_pin15), .pin11(out[15]),
    .pin12(out[14]), .pin13(out[13]), .pin14(out[12]), .pin16(1'b1));  // open: pin15
  // also tied to GND on the sheet: {_74163_1_pin3[0], _74163_1_pin3[1], _74163_1_pin3[2], _74163_1_pin3[3], _74163_1_pin3[4], _74163_1_pin3[5], _74163_1_pin3[6], _74163_1_pin3[7], _74163_3_pin3[0], _74163_3_pin3[1], _74163_3_pin3[2], _74163_3_pin3[3], _74163_3_pin3[4], _74163_3_pin3[5], _74163_3_pin3[6], _74163_3_pin3[7]}

  // Notes on the sheet:
  //   clk: Hz: 100
endmodule
