// Digital circuit state_char.dig as structural Verilog
module state_char (
  input  [7:0] D,
  input  drawing,
  input  clk,
  input  reset,
  input  en,
  output next,
  output done,
  output send,
  output fill
);

  wire and_1_out, and_2_out, and_5_out, not_1_out, not_2_out;

  not not_1 (not_1_out, D[0]);
  and and_1 (and_1_out, not_1_out, en);
  and and_2 (and_2_out, and_1_out, D[3]);
  and and_3 (next, and_2_out, D[1]);
  and and_4 (done, and_2_out, D[2]);
  and and_5 (and_5_out, and_2_out, D[4], drawing);
  not not_2 (not_2_out, D[3]);
  and and_6 (fill, and_1_out, not_2_out);
  JK_FF jk_ff_1 (.J(and_5_out), .C(clk), .K(reset), .Q(send));  // open: nQ
endmodule
